# Fritzing sketch Voltmeter Circuit (saved by Fritzing 0.9.2b)
circuit board: 8.40292cm x 6.6645cm
breadboards: 1

parts:
  Test_Voltage = Battery block 9V
  Part1 = Arduino Uno (Rev3)
  D1 = 1n4007 Diode [part_number=1N4007 package="300 mil [THT]"]
  R2 = Resistor [tolerance=±5% resistance=10k package=THT]
  R3 = Resistor [tolerance=±5% resistance=10k package=THT]

nets:
  N1: Test_Voltage.-, Part1.GND, R3.Pin_1
  N2: Test_Voltage.+, D1.anode
  N3: Part1.A0, R2.Pin_1, R3.Pin_0
  N4: D1.cathode, R2.Pin_0

custom parts:
  1n4007 Diode: "A standard rectifier diode". Originally by Brendan Howell.

// code stored in the sketch: voltmeter.ino
void setup() {
  // put your setup code here, to run once:
  pinMode(13,OUTPUT);
  Serial.begin(19200);
}

boolean battConnected = false;
static float DIODE_DROP = 0.48; // experimentally determined for 6/24/16's setup

/**
 * Battery voltage is run through a protection diode and then halved for measurement.
 * To correct this, we map the analog input value (from 0 to 1023) to nine volts, and
 * then add the voltage drop of our diode.
 * 
 * After processing, we then output it to serial.  When the battery is disconnected,
 * we output one blank line and wait for voltage to be applied again.
 */
void loop() {
  float rawIn = (float) analogRead(0);
  float vIn = fMap(rawIn, 0, 1023, 0, 9) + DIODE_DROP;
  
  if (vIn<=DIODE_DROP) {
    if (battConnected) {
      Serial.println();
      battConnected = false;
    }
  } else {
    Serial.print(vIn);
    Serial.println(" V");
    battConnected = true;
  }
  
  delay(100);
}

/**
 * This is the code behind the built-in map(), changed to work with floats.
 */
float fMap(float x, float in_min, float in_max, float out_min, float out_max)
{
  return (x - in_min) * (out_max - out_min) / (in_max - in_min) + out_min;
}
